// Logisim project 1.circ as structural Verilog: 1 circuit, main circuit main
module main (
);

  wire button_1_out, nand_1_out, nand_2_out, nand_3_out, nand_4_out, nand_5_out, nand_6_out, nand_7_out,
       nand_8_out, X1_q, X2_q, X2_qn, X3_q, X3_qn;

  Button button_1 (.out(button_1_out));
  T_Flip_Flop X1 (.T(button_1_out), .clk(X2_qn), .Q(X1_q));  // open: Qn, reset, preset
  T_Flip_Flop X2 (.T(button_1_out), .clk(X3_qn), .Q(X2_q), .Qn(X2_qn));  // open: reset, preset
  T_Flip_Flop X3 (.T(button_1_out), .clk(button_1_out), .Q(X3_q), .Qn(X3_qn));  // open: reset, preset
  nand nand_1 (nand_1_out, X2_q, X2_q);
  nand nand_2 (nand_2_out, X3_q, X3_q);
  nand nand_3 (nand_3_out, X1_q, nand_2_out);
  nand nand_4 (nand_4_out, nand_3_out, X2_q);
  nand nand_5 (nand_5_out, nand_1_out, nand_2_out);
  nand nand_6 (nand_6_out, nand_4_out, nand_8_out);
  LED led_1 (.in(nand_6_out));
  nand nand_7 (nand_7_out, nand_5_out, nand_5_out);
  nand nand_8 (nand_8_out, X1_q, nand_7_out);
endmodule
