// Logisim project 3.circ as structural Verilog: 1 circuit, main circuit main
module main (
);

  wire button_1_out, button_2_out, t_ff_1_q, t_ff_2_q, t_ff_3_q, t_ff_4_q, t_ff_5_q, t_ff_5_qn, t_ff_6_q,
       t_ff_6_qn, t_ff_7_q, t_ff_7_qn, t_ff_8_q;

  Button button_1 (.out(button_1_out));
  T_Flip_Flop t_ff_1 (.T(button_1_out), .clk(button_1_out), .Q(t_ff_1_q));  // open: Qn, reset, preset
  T_Flip_Flop t_ff_2 (.T(button_1_out), .clk(t_ff_1_q), .Q(t_ff_2_q));  // open: Qn, reset, preset
  T_Flip_Flop t_ff_3 (.T(button_1_out), .clk(t_ff_2_q), .Q(t_ff_3_q));  // open: Qn, reset, preset
  T_Flip_Flop t_ff_4 (.T(button_1_out), .clk(t_ff_3_q), .Q(t_ff_4_q));  // open: Qn, reset, preset
  LED A1 (.in(t_ff_1_q));
  LED A2 (.in(t_ff_2_q));
  LED A3 (.in(t_ff_3_q));
  LED A4 (.in(t_ff_4_q));
  T_Flip_Flop t_ff_5 (.T(button_2_out), .clk(button_2_out), .Q(t_ff_5_q), .Qn(t_ff_5_qn));  // open: reset, preset
  Button button_2 (.out(button_2_out));
  T_Flip_Flop t_ff_6 (.T(button_2_out), .clk(t_ff_5_qn), .Q(t_ff_6_q), .Qn(t_ff_6_qn));  // open: reset, preset
  T_Flip_Flop t_ff_7 (.T(button_2_out), .clk(t_ff_6_qn), .Q(t_ff_7_q), .Qn(t_ff_7_qn));  // open: reset, preset
  T_Flip_Flop t_ff_8 (.T(button_2_out), .clk(t_ff_7_qn), .Q(t_ff_8_q));  // open: Qn, reset, preset
  LED B1 (.in(t_ff_5_q));
  LED B2 (.in(t_ff_6_q));
  LED B3 (.in(t_ff_7_q));
  LED B4 (.in(t_ff_8_q));
endmodule
