// Logisim project 4.circ as structural Verilog: 2 circuits, main circuit main
module main (
);

  wire and_1_out, clock_1_out, dec_1_q0, dec_1_q1, dec_1_q2, dec_1_q3, dec_1_q4, dec_1_q5, dec_1_q6,
       dec_1_q7, dec_1_q8, dec_1_q9, dec_1_q10, dec_1_q11, t_ff_1_q, t_ff_1_qn, t_ff_2_q, t_ff_2_qn,
       t_ff_3_q, t_ff_3_qn, t_ff_4_q;

  T_Flip_Flop t_ff_1 (
    .T(clock_1_out), .clk(clock_1_out), .Q(t_ff_1_q), .Qn(t_ff_1_qn), .reset(and_1_out));  // open: preset
  Clock clock_1 (.out(clock_1_out));
  T_Flip_Flop t_ff_2 (
    .T(clock_1_out), .clk(t_ff_1_qn), .Q(t_ff_2_q), .Qn(t_ff_2_qn), .reset(and_1_out));  // open: preset
  T_Flip_Flop t_ff_3 (
    .T(clock_1_out), .clk(t_ff_2_qn), .Q(t_ff_3_q), .Qn(t_ff_3_qn), .reset(and_1_out));  // open: preset
  T_Flip_Flop t_ff_4 (.T(clock_1_out), .clk(t_ff_3_qn), .Q(t_ff_4_q), .reset(and_1_out));  // open: Qn, preset
  and and_1 (and_1_out, ~t_ff_1_q, ~t_ff_2_q, t_ff_3_q, t_ff_4_q);  // AND_Gate
  LED led_1 (.in(dec_1_q0));
  dec dec_1 (
    .A1(t_ff_1_q), .A2(t_ff_2_q), .A3(t_ff_3_q), .A4(t_ff_4_q), .Q0(dec_1_q0), .Q1(dec_1_q1), .Q2(dec_1_q2),
    .Q3(dec_1_q3), .Q4(dec_1_q4), .Q5(dec_1_q5), .Q6(dec_1_q6), .Q7(dec_1_q7), .Q8(dec_1_q8), .Q9(dec_1_q9),
    .Q10(dec_1_q10), .Q11(dec_1_q11));
  LED led_2 (.in(dec_1_q1));
  LED led_3 (.in(dec_1_q2));
  LED led_4 (.in(dec_1_q3));
  LED led_5 (.in(dec_1_q4));
  LED led_6 (.in(dec_1_q5));
  LED led_7 (.in(dec_1_q6));
  LED led_8 (.in(dec_1_q7));
  LED led_9 (.in(dec_1_q8));
  LED led_10 (.in(dec_1_q9));
  LED led_11 (.in(dec_1_q10));
  LED led_12 (.in(dec_1_q11));
endmodule

module dec (
  input  A1,
  input  A2,
  input  A3,
  input  A4,
  output Q0,
  output Q1,
  output Q2,
  output Q3,
  output Q4,
  output Q5,
  output Q6,
  output Q7,
  output Q8,
  output Q9,
  output Q10,
  output Q11
);

  wire not_1_out, not_2_out, not_3_out, not_4_out;

  not not_1 (not_1_out, A1);
  not not_2 (not_2_out, A2);
  not not_3 (not_3_out, A3);
  not not_4 (not_4_out, A4);
  and and_1 (Q1, A1, not_2_out, not_3_out, not_4_out);
  and and_2 (Q3, A1, A2, not_3_out, not_4_out);
  and and_3 (Q5, A1, not_2_out, A3, not_4_out);
  and and_4 (Q7, A1, A2, A3, not_4_out);
  and and_5 (Q9, A1, not_2_out, not_3_out, A4);
  and and_6 (Q11, A1, A2, not_3_out, A4);
  and and_7 (Q0, not_1_out, not_2_out, not_3_out, not_4_out);
  and and_8 (Q2, not_1_out, A2, not_3_out, not_4_out);
  and and_9 (Q4, not_1_out, not_2_out, A3, not_4_out);
  and and_10 (Q6, not_1_out, A2, A3, not_4_out);
  and and_11 (Q8, not_1_out, not_2_out, not_3_out, A4);
  and and_12 (Q10, not_1_out, A2, not_3_out, A4);
endmodule
