// Logisim project 5.circ as structural Verilog: 2 circuits, main circuit main
module main (
);

  wire and_1_out, clock_1_out, dec_1_a, dec_1_b, dec_1_c, dec_1_d, dec_1_e, dec_1_f, dec_1_g, t_ff_1_q,
       t_ff_1_qn, t_ff_2_q, t_ff_2_qn, t_ff_3_q, t_ff_3_qn, t_ff_4_q;

  Clock clock_1 (.out(clock_1_out));
  and and_1 (and_1_out, t_ff_4_q, ~t_ff_3_q, t_ff_2_q, ~t_ff_1_q);  // AND_Gate
  T_Flip_Flop t_ff_1 (.T(1'b1), .clk(clock_1_out), .Q(t_ff_1_q), .Qn(t_ff_1_qn), .reset(and_1_out));  // open: preset
  T_Flip_Flop t_ff_2 (.T(1'b1), .clk(t_ff_1_qn), .Q(t_ff_2_q), .Qn(t_ff_2_qn), .reset(and_1_out));  // open: preset
  dec dec_1 (
    .X1(t_ff_4_q), .X2(t_ff_3_q), .X3(t_ff_2_q), .X4(t_ff_1_q), .A(dec_1_a), .B(dec_1_b), .C(dec_1_c),
    .D(dec_1_d), .E(dec_1_e), .F(dec_1_f), .G(dec_1_g));
  T_Flip_Flop t_ff_3 (.T(1'b1), .clk(t_ff_2_qn), .Q(t_ff_3_q), .Qn(t_ff_3_qn), .reset(and_1_out));  // open: preset
  T_Flip_Flop t_ff_4 (.T(1'b1), .clk(t_ff_3_qn), .Q(t_ff_4_q), .reset(and_1_out));  // open: Qn, preset
  _7_Segment_Display #(.decimalPoint("false")) u_7_segment_display_1 (
    .g(dec_1_g), .f(dec_1_f), .a(dec_1_a), .b(dec_1_b), .e(dec_1_e), .d(dec_1_d), .c(dec_1_c));
endmodule

module dec (
  input  X1,
  input  X2,
  input  X3,
  input  X4,
  output A,
  output B,
  output C,
  output D,
  output E,
  output F,
  output G
);

  wire and_1_out, and_2_out, and_3_out, and_4_out, Ax_out, Bx_out, Cx_out, Dx_out, Ex_out, not_1_out,
       not_2_out, not_3_out, not_4_out;

  not not_1 (not_1_out, X1);
  not not_2 (not_2_out, X2);
  not not_3 (not_3_out, X3);
  not not_4 (not_4_out, X4);
  and Ax (Ax_out, not_2_out, not_4_out);
  and Bx (Bx_out, not_3_out, not_4_out);
  and Cx (Cx_out, X3, not_4_out);
  and Dx (Dx_out, not_2_out, X3);
  and Ex (Ex_out, X2, not_3_out);
  and and_1 (and_1_out, X2, X4);
  and and_2 (and_2_out, X3, X4);
  and and_3 (and_3_out, X2, not_3_out, X4);
  and and_4 (and_4_out, X2, not_4_out);
  or or_1 (A, Ax_out, and_1_out, X1, X3);
  or or_2 (B, Bx_out, and_2_out, not_2_out);
  or or_3 (C, X2, not_3_out, X4);
  or or_4 (D, Ax_out, Cx_out, and_3_out, Dx_out, X1);
  or or_5 (E, Ax_out, Cx_out);
  or or_6 (F, Bx_out, and_4_out, Ex_out, X1);
  or or_7 (G, Dx_out, Ex_out, Cx_out, X1);

  // Notes on the sheet:
  //   Ax=~X2^~X4
  //   Bx=~X3^~X4
  //   Cx=  X3^~X4
  //   Dx=~X2^  X3
  //   Ex=  X2^~X3
endmodule
