// Logisim project 7.circ as structural Verilog
module counter0 (
  input  A1,
  input  A2,
  input  A3,
  input  A4,
  input  A5,
  input  A6,
  input  A7,
  input  A8
);

  T_Flip_Flop t_ff_1 ();  // open: T, clk, Q, Qn, reset, preset
endmodule
